# Fritzing sketch sketch_003Snake (saved by Fritzing 0.9.3b)
breadboards: 1

parts:
  J1 = STM32 Nucleo boards
  S1 = Pushbutton [package="[SMD]"]
  S2 = Pushbutton [package="[SMD]"]
  S3 = Pushbutton [package="[SMD]"]
  S4 = Pushbutton [package="[SMD]"]
  Disp1 = LBT2088AH [part_number=LBT2088AH]
  J2 = shrouded pin header, 16 pins [form="♂ (shrouded male)"]
  J3 = shrouded pin header, 16 pins [form="♂ (shrouded male)"]
  R1 = Resistor [tolerance=±5% resistance=270 package="0402 [SMD]"]
  R2 = Resistor [tolerance=±5% resistance=270 package="0402 [SMD]"]
  R3 = Resistor [tolerance=±5% resistance=270 package="0402 [SMD]"]
  R4 = Resistor [tolerance=±5% resistance=270 package="0402 [SMD]"]
  R5 = Resistor [tolerance=±5% resistance=270 package="0402 [SMD]"]
  R6 = Resistor [tolerance=±5% resistance=270 package="0402 [SMD]"]
  R7 = Resistor [tolerance=±5% resistance=270 package="0402 [SMD]"]
  R8 = Resistor [tolerance=±5% resistance=270 package="0402 [SMD]"]

nets:
  N1: J1.PA11, J3.pin8
  N2: J1.PB12, J3.pin7
  N3: J1.D8, J3.pin16
  N4: J1.D9_PWM, J3.pin15
  N5: J1.D10_PWM/SS, J3.pin14
  N6: J1.D11_PWM/MOSI, J3.pin13
  N7: J1.D12/MISO, J3.pin12
  N8: J1.D13/SCK, J3.pin11
  N9: J1.A4/SDA, J3.pin10
  N10: J1.A5/SCL, J3.pin9
  N11: J1.D3_PWM, S1.Pin_3, S1.Pin_4
  N12: J1.D5_PWM, S4.Pin_3, S4.Pin_4
  N13: J1.D6_PWM, S2.Pin_3, S2.Pin_4
  N14: J1.D7, S3.Pin_3, S3.Pin_4
  N15: J1.GND, S1.Pin_1, S1.Pin_2, S3.Pin_1, S3.Pin_2, S4.Pin_1, S4.Pin_2
  N16: J1.PB2, J3.pin6
  N17: J1.PB1, J3.pin5
  N18: J1.PB15, J3.pin4
  N19: J1.PB14, J3.pin3
  N20: J1.PB13, J3.pin2
  N21: J1.PC4, J3.pin1
  N22: S2.Pin_1, S2.Pin_2
  N23: Disp1.pin1, R4.Pin_1
  N24: Disp1.pin2, R7.Pin_1
  N25: Disp1.pin_3, J2.pin7
  N26: Disp1.pin_4, J2.pin6
  N27: Disp1.pin_5, R3.Pin_1
  N28: Disp1.pin_6, J2.pin4
  N29: Disp1.pin_7, R5.Pin_1
  N30: Disp1.pin_8, R6.Pin_1
  N31: Disp1.pin_9, R1.Pin_1
  N32: Disp1.pin_10, J2.pin5
  N33: Disp1.pin_11, J2.pin3
  N34: Disp1.pin_12, R8.Pin_1
  N35: Disp1.pin_13, J2.pin8
  N36: Disp1.pin_14, R2.Pin_1
  N37: Disp1.pin_15, J2.pin2
  N38: Disp1.pin_16, J2.pin1
  N39: J2.pin9, R1.Pin_0
  N40: J2.pin10, R2.Pin_0
  N41: J2.pin11, R6.Pin_0
  N42: J2.pin12, R8.Pin_0
  N43: J2.pin13, R4.Pin_0
  N44: J2.pin14, R5.Pin_0
  N45: J2.pin15, R7.Pin_0
  N46: J2.pin16, R3.Pin_0

notes:
  J2 и J3 это один элемент
